// Logisim project Tucano-8.circ as structural Verilog: 15 circuits, main circuit Registers
module Registers (
  input  [7:0] WriteData,
  input  RegWrite,
  input  [1:0] rd,
  input  [1:0] rs,
  input  CLK,
  input  RST,
  output [7:0] rd_out,
  output [7:0] rs_out
);

  wire demultiplexer_1_out0, demultiplexer_1_out1, demultiplexer_1_out2, demultiplexer_1_out3;
  wire [7:0] r0_q, r1_q, r2_q, r3_q;

  Demultiplexer #(.select(2)) demultiplexer_1 (
    .out0(demultiplexer_1_out0), .out1(demultiplexer_1_out1), .out2(demultiplexer_1_out2),
    .out3(demultiplexer_1_out3), .in(RegWrite), .sel(rd));
  Register r0 (.D(WriteData), .en(demultiplexer_1_out0), .clk(CLK), .Q(r0_q), .clr(RST));
  Register r1 (.D(WriteData), .en(demultiplexer_1_out1), .clk(CLK), .Q(r1_q), .clr(RST));
  Register r2 (.D(WriteData), .en(demultiplexer_1_out2), .clk(CLK), .Q(r2_q), .clr(RST));
  Register r3 (.D(WriteData), .en(demultiplexer_1_out3), .clk(CLK), .Q(r3_q), .clr(RST));
  Multiplexer #(.select(2), .width(8)) multiplexer_1 (
    .in0(r0_q), .in1(r1_q), .in2(r2_q), .in3(r3_q), .out(rd_out), .sel(rd));
  Multiplexer #(.select(2), .width(8)) multiplexer_2 (
    .in0(r0_q), .in1(r1_q), .in2(r2_q), .in3(r3_q), .out(rs_out), .sel(rs));
endmodule

module ALU (
  input  [7:0] RD,
  input  [7:0] RS,
  input  [3:0] Opcode,
  input  FlagWrite,
  input  CLK,
  output [7:0] alu_out,
  output Flag
);

  wire comparator_1_eq, comparator_1_gt, comparator_1_lt, comparator_2_eq;
  wire [7:0] adder_1_out, and_1_out, bit_extender_1_out, bit_extender_2_out, bit_extender_3_out, not_1_out,
       or_1_out, shifter_1_out, shifter_2_out, subtractor_1_out;

  Adder adder_1 (.a(RD), .b(RS), .out(adder_1_out));  // open: cin, cout
  Subtractor subtractor_1 (.a(RD), .b(RS), .out(subtractor_1_out));  // open: bin, bout
  assign and_1_out = RD & RS;  // AND_Gate and_1, 8 bits wide
  assign or_1_out = RD | RS;  // OR_Gate or_1, 8 bits wide
  assign not_1_out = ~RD;  // NOT_Gate not_1, 8 bits wide
  Shifter shifter_1 (.in(RD), .\dist (3'b001), .out(shifter_1_out));
  Shifter #(.shift("lr")) shifter_2 (.in(RD), .\dist (3'b001), .out(shifter_2_out));
  Comparator comparator_1 (.a(RD), .b(RS), .gt(comparator_1_gt), .eq(comparator_1_eq), .lt(comparator_1_lt));
  assign bit_extender_1_out = {{7{1'b0}}, comparator_1_lt};  // Bit_Extender bit_extender_1
  assign bit_extender_2_out = {{7{1'b0}}, comparator_1_gt};  // Bit_Extender bit_extender_2
  Multiplexer #(.select(4), .width(8)) multiplexer_1 (
    .in0(adder_1_out), .in1(subtractor_1_out), .in2(and_1_out), .in3(or_1_out), .in4(not_1_out),
    .in5(shifter_1_out), .in6(shifter_2_out), .in7(bit_extender_2_out), .in8(bit_extender_1_out),
    .in9(bit_extender_3_out), .in10({8{1'b0}}), .in11({8{1'b0}}), .in12({8{1'b0}}),
    .in13({4'b0000, RS[3:0]}), .in14({8{1'b0}}), .in15({8{1'b0}}), .out(alu_out), .sel(Opcode));
  assign bit_extender_3_out = {{7{1'b0}}, comparator_1_eq};  // Bit_Extender bit_extender_3
  Comparator comparator_2 (.a(alu_out), .b({8{1'b0}}), .eq(comparator_2_eq));  // open: gt, lt
  Register #(.width(1)) register_1 (.D(comparator_2_eq), .en(FlagWrite), .clk(CLK), .Q(Flag));  // open: clr
endmodule

module UC (
  input  [3:0] Opcode,
  output MemRead,
  output MemWrite,
  output RegWrite,
  output ALUSrc,
  output BEQ,
  output BNE,
  output MemToReg,
  output FlagWrite,
  output Jump
);

  MemReadUC memreaduc_1 (.Opcode(Opcode), .MemRead(MemRead));
  MemWriteUC memwriteuc_1 (.Opcode(Opcode), .MemWrite(MemWrite));
  RegWriteUC regwriteuc_1 (.Opcode(Opcode), .RegWrite_out(RegWrite));
  ALUSrcUC alusrcuc_1 (.Opcode(Opcode), .ALUSrc(ALUSrc));
  BranchUC branchuc_1 (.Opcode(Opcode), .BeqEnable(BEQ), .BneEnable(BNE));
  MemToRegUC memtoreguc_1 (.Opcode(Opcode), .MemToReg(MemToReg));
  FlagWriteUC flagwriteuc_1 (.Opcode(Opcode), .FlagWrite_out(FlagWrite));
  jumpUC jumpuc_1 (.Opcode(Opcode), .Jump(Jump));
endmodule

module RAM_8b (
  input  [7:0] Address,
  input  MemWrite,
  input  MemRead,
  input  CLK,
  input  [7:0] Din,
  output [7:0] Dout
);

  wire [7:0] ram_1_dout;

  RAM #(.asyncread("true")) ram_1 (
    .addr(Address), .we(MemWrite), .oe(MemRead), .clk(CLK), .din(Din), .dout(ram_1_dout));
  Demultiplexer #(.width(8)) demultiplexer_1 (.out1(Dout), .in(ram_1_dout), .sel(MemRead));  // open: out0
endmodule

module ROM_8b (
  input  [7:0] PC,
  output [7:0] op
);

  ROM rom_1 (.addr(PC), .data(op));

  // Notes on the sheet:
  //   contents of rom_1 (hex, n*v repeats v):
  //   11 c3 0 0 0 40
endmodule

module jumpUC (
  input  [3:0] Opcode,
  output Jump
);

  Decoder #(.select(4)) decoder_1 (
    .out10(Jump), .sel(Opcode));  // open: out0, out1, out2, out3, out4, out5, out6, out7, out8, out9, out11, out12, out13, out14, out15, en
endmodule

module MemReadUC (
  input  [3:0] Opcode,
  output MemRead
);

  Decoder #(.select(4)) decoder_1 (
    .out14(MemRead), .sel(Opcode));  // open: out0, out1, out2, out3, out4, out5, out6, out7, out8, out9, out10, out11, out12, out13, out15, en
endmodule

module MemWriteUC (
  input  [3:0] Opcode,
  output MemWrite
);

  Decoder #(.select(4)) decoder_1 (
    .out15(MemWrite), .sel(Opcode));  // open: out0, out1, out2, out3, out4, out5, out6, out7, out8, out9, out10, out11, out12, out13, out14, en
endmodule

module RegWriteUC (
  input  [3:0] Opcode,
  output RegWrite_out
);

  wire decoder_1_out0, decoder_1_out1, decoder_1_out2, decoder_1_out3, decoder_1_out4, decoder_1_out5,
       decoder_1_out6, decoder_1_out14;

  Decoder #(.select(4)) decoder_1 (
    .out0(decoder_1_out0), .out1(decoder_1_out1), .out2(decoder_1_out2), .out3(decoder_1_out3),
    .out4(decoder_1_out4), .out5(decoder_1_out5), .out6(decoder_1_out6), .out14(decoder_1_out14), .sel(Opcode));  // open: out7, out8, out9, out10, out11, out12, out13, out15, en
  or or_1 (RegWrite_out, decoder_1_out0, decoder_1_out1, decoder_1_out2, decoder_1_out3, decoder_1_out4, decoder_1_out5, decoder_1_out6, decoder_1_out14);
endmodule

module ALUSrcUC (
  input  [3:0] Opcode,
  output ALUSrc
);

  wire decoder_1_out11, decoder_1_out12, decoder_1_out14, decoder_1_out15;

  Decoder #(.select(4)) decoder_1 (
    .out11(decoder_1_out11), .out12(decoder_1_out12), .out14(decoder_1_out14), .out15(decoder_1_out15),
    .sel(Opcode));  // open: out0, out1, out2, out3, out4, out5, out6, out7, out8, out9, out10, out13, en
  or or_1 (ALUSrc, decoder_1_out11, decoder_1_out12, decoder_1_out14, decoder_1_out15);
endmodule

module PCWriteUC (
  input  n4,
  input  n5,
  input  n6,
  input  n7,
  output PCWrite
);

  wire beq_out, bne_out, Jump_out, not_1_out, not_2_out, not_3_out, not_4_out, not_5_out;

  not not_1 (not_1_out, n4);
  not not_2 (not_2_out, n6);
  not not_3 (not_3_out, n6);
  not not_4 (not_4_out, n4);
  not not_5 (not_5_out, n5);
  and Jump (Jump_out, not_1_out, n5, not_2_out, n7);
  and beq (beq_out, n4, n5, not_3_out, n7);
  and bne (bne_out, not_4_out, not_5_out, n6, n7);
  or or_1 (PCWrite, Jump_out, beq_out, bne_out);
endmodule

module BranchUC (
  input  [3:0] Opcode,
  output BeqEnable,
  output BneEnable
);

  Decoder #(.select(4)) decoder_1 (
    .out11(BeqEnable), .out12(BneEnable), .sel(Opcode));  // open: out0, out1, out2, out3, out4, out5, out6, out7, out8, out9, out10, out13, out14, out15, en
endmodule

module MemToRegUC (
  input  [3:0] Opcode,
  output MemToReg
);

  Decoder #(.select(4)) decoder_1 (
    .out14(MemToReg), .sel(Opcode));  // open: out0, out1, out2, out3, out4, out5, out6, out7, out8, out9, out10, out11, out12, out13, out15, en
endmodule

module Main (
  input  RST,
  output [7:0] out_2,
  output [7:0] out_3,
  output [7:0] out_4,
  output [7:0] out_5,
  output [7:0] out_6,
  output [7:0] out_7
);

  wire alu_1_flag, ALUSrc, BEQ, beq_out, BNE, bne_out, branch_out, CLK, FlagWrite, Jump, MemRead, MemToReg,
       MemWrite, not_1_out, RegWrite;
  wire [7:0] adder_1_out, adder_2_out, multiplexer_2_out, multiplexer_3_out, PC_q, ram_8b_1_dout,
       registers_1_rd_out;

  Multiplexer #(.width(8)) multiplexer_1 (.in0(multiplexer_2_out), .in1(out_2), .out(out_6), .sel(Jump));
  Register PC (.D(out_6), .en(1'b1), .clk(CLK), .Q(PC_q), .clr(RST));
  not not_1 (not_1_out, alu_1_flag);
  and u_bne (bne_out, BNE, not_1_out);
  and u_beq (beq_out, BEQ, alu_1_flag);
  or branch (branch_out, bne_out, beq_out);
  Multiplexer #(.width(8)) multiplexer_2 (
    .in0(adder_1_out), .in1(adder_2_out), .out(multiplexer_2_out), .sel(branch_out));
  Adder adder_1 (.a(8'h1), .b(PC_q), .out(adder_1_out));  // open: cin, cout
  Adder adder_2 (.a(out_2), .b(PC_q), .out(adder_2_out));  // open: cin, cout
  ROM_8b rom_8b_1 (.PC(PC_q), .op(out_5));
  Clock u_CLK (.out(CLK));
  assign out_2 = {{4{1'b0}}, out_5[3:0]};  // Bit_Extender bit_extender_1
  Registers registers_1 (
    .WriteData(out_3), .RegWrite(RegWrite), .rd(out_5[3:2]), .rs(out_5[1:0]), .CLK(CLK), .RST(RST),
    .rd_out(registers_1_rd_out), .rs_out(out_7));
  Multiplexer #(.width(8)) multiplexer_3 (.in0(out_7), .in1(out_2), .out(multiplexer_3_out), .sel(ALUSrc));
  UC uc_1 (
    .Opcode(out_5[7:4]), .MemRead(MemRead), .MemWrite(MemWrite), .RegWrite(RegWrite), .ALUSrc(ALUSrc),
    .BEQ(BEQ), .BNE(BNE), .MemToReg(MemToReg), .FlagWrite(FlagWrite), .Jump(Jump));
  Multiplexer #(.width(8)) multiplexer_4 (.in0(out_4), .in1(ram_8b_1_dout), .out(out_3), .sel(MemToReg));
  ALU alu_1 (
    .RD(registers_1_rd_out), .RS(multiplexer_3_out), .Opcode(out_5[7:4]), .FlagWrite(FlagWrite), .CLK(CLK),
    .alu_out(out_4), .Flag(alu_1_flag));
  RAM_8b ram_8b_1 (
    .Address(out_2), .MemWrite(MemWrite), .MemRead(MemRead), .CLK(CLK), .Din(out_7), .Dout(ram_8b_1_dout));

  // Other names for the same wires on the sheet: address[7:0] = out_2; Opcode[3:0] = out_5[7:4]
endmodule

module FlagWriteUC (
  input  [3:0] Opcode,
  output FlagWrite_out
);

  wire decoder_1_out0, decoder_1_out1, decoder_1_out2, decoder_1_out3, decoder_1_out4, decoder_1_out5,
       decoder_1_out6;

  Decoder #(.select(4)) decoder_1 (
    .out0(decoder_1_out0), .out1(decoder_1_out1), .out2(decoder_1_out2), .out3(decoder_1_out3),
    .out4(decoder_1_out4), .out5(decoder_1_out5), .out6(decoder_1_out6), .sel(Opcode));  // open: out7, out8, out9, out10, out11, out12, out13, out14, out15, en
  or or_1 (FlagWrite_out, decoder_1_out0, decoder_1_out1, decoder_1_out2, decoder_1_out3, decoder_1_out4, decoder_1_out5, decoder_1_out6);
endmodule
